# Fritzing sketch electronique_bateau-gyro (saved by Fritzing 0.8.7b)
breadboards: 1

parts:
  Part1 = Arduino Uno (Rev3)
  C1 = Electrolytic Capacitor [capacitance=100µF package="200 mil [THT, electrolytic]"]
  C2 = Electrolytic Capacitor [capacitance=100µF package="200 mil [THT, electrolytic]"]  # not connected
  J1 = Basic Servo
  J2 = Basic Servo
  VCC2 = Battery block 9V
  Part2 = InvenSense MPU6050
  VCC3 = Battery
  VCC4 = Battery  # not connected
  Transceiver1 = nRF24L01 [package=module]
  DC_Mot_Enc1 = DC Motor with two-phase hall-encoder [part_number=VT-E-G25A-06-177E]

nets:
  N1: Part1.A4/SDA, Part2.SDA
  N2: Part1.A5/SCL, Part2.SCL
  N3: Part1.D9_PWM, Transceiver1.CE
  N4: Part1.D10_PWM/SS, Transceiver1.CSN
  N5: Part1.D11_PWM/MOSI, Transceiver1.MOSI
  N6: Part1.D12/MISO, Transceiver1.MISO
  N7: Part1.D13/SCK, Transceiver1.SCK
  N8: Part1.D2, DC_Mot_Enc1.pin4
  N9: Part1.D3_PWM, DC_Mot_Enc1.pin3
  N10: Part1.D5_PWM, J1.pulse
  N11: Part1.D6_PWM, J2.pulse
  VCC: Part1.3V3, Part2.VCC, Transceiver1.VCC, DC_Mot_Enc1.pin1
  GND: Part1.GND, C1.-, J1.gnd, J2.gnd, VCC2.-, Part2.GND, VCC3.-, Transceiver1.GND, DC_Mot_Enc1.pin2
  N12: Part1.VIN, VCC2.+
  VCC_2: C1.+, J1.vcc, J2.vcc, VCC3.+

notes:
  Servo barre
  pin 7 Arduino
  Servo ecoute
  pin 6 Arduino
  Module Gyro GY 521
  SCL // A5
  SCA // A4
  Module Radio
  Alimente en 3,3V!
  MR // Arduino
  CE // PIN 9
  SCLK // PIN 13
  MISO // PIN 12
  CSN // PIN 10
  MOSI // PIN 11
  Encodeur
  OUT B // Pin 2
  OUT A // Pin 3

custom parts:
  nRF24L01: nRF24L01 module
